# Fritzing sketch 555 (saved by Fritzing 0.9.1b)
breadboards: 1

parts:
  U1 = 555 Timer [package="DIP8 [THT]"]
  R1 = Resistor [tolerance=±5% resistance=22 package="1206 [SMD]"]
  R2 = Resistor [tolerance=±5% resistance=22 package="1206 [SMD]"]
  C1 = Ceramic Capacitor [capacitance=10nF package="200 mil [THT, multilayer]"]
  C2 = Electrolytic Capacitor [capacitance=0.1mF package="100 mil [THT, electrolytic]"]
  LED1 = smd LED [color="Red (633nm)" package="0603 [SMD]"]
  R3 = Resistor [tolerance=±5% resistance=330 package="0805 [SMD]"]
  VCC1 = Battery block 9V

nets:
  N1: U1.Ground, C1.1, C2.-, LED1.cathode, VCC1.-
  N2: U1.Trigger, U1.Threshold, R2.Pin_0, C2.+
  N3: U1.Output, R3.Pin_0
  N4: U1.Reset, U1.Vcc_Supply_Voltage, R1.Pin_1, VCC1.+
  N5: U1.Control_Voltage, C1.0
  N6: U1.Discharge, R1.Pin_0, R2.Pin_1
  N7: LED1.anode, R3.Pin_1
